# Fritzing sketch Circuit-Diagram (saved by Fritzing 0.9.3b)
breadboards: 1

parts:
  BATT1 = 4xAA Switchable Battery Pack w/Bare Wire
  Raspberry_Pi_1 = Raspberry Pi 3 [part_number=RPI-3-V1.2]
  S1 = H-Bridge with L298N
  LED1 = LED - 5mm [color="Red (633nm)" package="5 mm [THT]"]
  R1 = Resistor [tolerance=±5% resistance=220 package=THT]
  M1 = DC Motor

nets:
  N1: BATT1.POS, S1.12V
  GND: BATT1.NEG, Raspberry_Pi_1.GND, S1.GND, R1.Pin_0
  N2: Raspberry_Pi_1.GIPO4, LED1.anode
  N3: Raspberry_Pi_1.GIPO17, S1.IN1
  N4: Raspberry_Pi_1.GIPO27, S1.IN2
  N5: S1.M1-01, M1.pin_2
  N6: S1.M1-02, M1.pin_1

custom parts:
  4xAA Switchable Battery Pack w/Bare Wire: 4xAA Switchable Battery Pack with Bare Wire connection
  H-Bridge with L298N: h-bridge
